# Fritzing sketch p3 (saved by Fritzing 1.0.1rc)
breadboards: 1

parts:
  Componente1 = Black Joystick KY-023
  Componente5 = Arduino Uno (Rev3) - ICSP
  LCD3 = LCD screen
  LED5 = LED - 3mm [color="Blue (430nm)" current=0.030 package="3 mm [THT]"]
  LED6 = LED - 3mm [color="Yellow (585nm)" current=0.030 package="3 mm [THT]"]
  S3 = Pushbutton [package="[THT]"]
  HC-SR04_Sensor_3 = HC-SR04 Ultrasonic Distance Sensor
  R9 = Resistor [tolerance=±5% power=0.25 resistance=220 package=THT]
  R10 = Rotary Potentiometer (Large) [maximum_resistance=100kΩ knob_status=50% package=THT]
  R11 = Resistor [tolerance=±5% power=0.25 resistance=220 package=THT]
  R12 = Resistor [tolerance=±5% power=0.25 resistance=220 package=THT]
  DHT2 = DHT11 Humitidy and Temperature Sensor (3 pins)

nets:
  N1: Componente1.SW, Componente5.D3_PWM
  N2: Componente1.VRy, Componente5.A0
  N3: Componente1.VRx, Componente5.A1
  +5V: Componente1.+5V, Componente5.5V, LCD3.VDD, HC-SR04_Sensor_3.VCC, R11.Pin_1, DHT2.Signal
  GND: Componente1.GND, Componente5.GND, LCD3.VSS, LCD3.R/W, LCD3.LED-, LED5.cathode, LED6.cathode, S3.Pin_1, S3.Pin_2, HC-SR04_Sensor_3.GND, R10.leg1, R10.leg2, DHT2.Gnd
  N4: Componente5.A4/SDA, HC-SR04_Sensor_3.ECHO
  N5: Componente5.ICSP_MISO, Componente5.D12/MISO, LCD3.RS
  N6: Componente5.D8, LCD3.DB5
  N7: Componente5.D9_PWM, LCD3.DB6
  N8: Componente5.D10_PWM/SS, LCD3.DB7
  N9: Componente5.D11_PWM/MOSI, LCD3.E
  N10: Componente5.D2, S3.Pin_3, S3.Pin_4
  N11: Componente5.D4, DHT2.Plus
  N12: Componente5.D5_PWM, HC-SR04_Sensor_3.TRIG
  N13: Componente5.D6_PWM, R12.Pin_0
  N14: Componente5.D7, LCD3.DB4
  N15: LCD3.V0, R10.wiper
  N16: LCD3.LED+, R11.Pin_0
  N17: LED5.anode, R9.Pin_0

custom parts:
  Black Joystick KY-023: Description: The joystick is a combination of 2 analoog potentiometer and a digital switch. Arduino GND --> Module pin - Arduino +5V --> Module pin +5V Arduino Analoog 0 --> Module VRx Arduino Analoog 1 --> Module VRy Arduino Digital --> Module SW Dimensions: 1" x 1.25"
  DHT11 Humitidy and Temperature Sensor (3 pins): DHT11 Humidity and Temperature Sensor (3 pins).
